// Logisim project riscv_logisim.circ as structural Verilog: 8 circuits, main circuit main
module main (
);

  wire Clk;
  wire [7:0] bit_extender_1_out;
  wire [31:0] Instruction, PC, shifter_1_out;

  Clock clock_1 (.out(Clk));
  Shifter #(.shift("lr"), .width(32)) shifter_1 (.in(PC), .\dist (5'b00010), .out(shifter_1_out));
  ROM #(.dataWidth(32)) rom_1 (.addr(bit_extender_1_out), .data(Instruction));
  Bit_Extender #(.in_width(32), .out_width(8), .\type ("zero")) bit_extender_1 (
    .in(shifter_1_out), .out(bit_extender_1_out));
  CPU cpu_1 (.Instruction(Instruction), .Clk(Clk), .PC(PC));

  // Notes on the sheet:
  //   contents of rom_1 (hex, n*v repeats v):
  //   6f
endmodule

module CPU (
  input  [31:0] Instruction,
  input  Clk,
  output [31:0] PC
);

  wire ALUArithmeticRightShift, ALUCompResult, ALUSub, MemLoad, MemStore, SetPcLSBTo0, Use0ForALU_RS1,
       Use0ForRD, UseImm, UseMemInForRD_Data, UsePcForALU_RS1, UsePcPlus4ForRD_Data;
  wire [2:0] ALUCompOp, ALUOperation;
  wire [4:0] multiplexer_2_out;
  wire [7:0] bit_extender_1_out;
  wire [31:0] ALUOutput, and_1_out, immgen_1_immout, MemExtended, MemInput, multiplexer_1_out,
       multiplexer_3_out, multiplexer_4_out, multiplexer_5_out, multiplexer_6_out, multiplexer_7_out,
       multiplexer_8_out, not_1_out, PC_plus_4, R1, R2;

  Bit_Extender #(.in_width(32), .out_width(8), .\type ("zero")) bit_extender_1 (
    .in(ALUOutput), .out(bit_extender_1_out));
  RAM #(.dataWidth(32)) ram_1 (
    .addr(bit_extender_1_out), .we(MemStore), .oe(MemLoad), .clk(Clk), .din(R2), .dout(MemInput));
  Adder #(.width(32)) adder_1 (.a(PC), .b(32'h4), .out(PC_plus_4));  // open: cin, cout
  Multiplexer #(.width(32)) multiplexer_1 (
    .in0(PC_plus_4), .in1(ALUOutput), .out(multiplexer_1_out), .sel(ALUCompResult));
  Multiplexer #(.width(5)) multiplexer_2 (
    .in0(Instruction[11:7]), .in1({5{1'b0}}), .out(multiplexer_2_out), .sel(Use0ForRD));
  assign not_1_out = ~32'h1;  // NOT_Gate not_1, 32 bits wide
  Multiplexer #(.width(32)) multiplexer_3 (
    .in0(multiplexer_1_out), .in1(and_1_out), .out(multiplexer_3_out), .sel(SetPcLSBTo0));
  assign and_1_out = multiplexer_1_out & not_1_out;  // AND_Gate and_1, 32 bits wide
  Multiplexer #(.width(32)) multiplexer_4 (
    .in0(ALUOutput), .in1(MemExtended), .out(multiplexer_4_out), .sel(UseMemInForRD_Data));
  Multiplexer #(.width(32)) multiplexer_5 (
    .in0(multiplexer_4_out), .in1(PC_plus_4), .out(multiplexer_5_out), .sel(UsePcPlus4ForRD_Data));
  ExtendMemInput extendmeminput_1 (.Instruction(Instruction), .MemIn(MemInput), .MemExtended(MemExtended));
  Register #(.width(32)) ProgramCounter (.D(multiplexer_3_out), .en(1'b1), .clk(Clk), .Q(PC));  // open: clr
  ControlLogic controllogic_1 (
    .Instruction(Instruction), .ALUOp(ALUOperation), .UseImm(UseImm),
    .ALUArithmeticShift(ALUArithmeticRightShift), .ALUSub(ALUSub), .MemLoad(MemLoad),
    .UseMemInForRD_Data(UseMemInForRD_Data), .UsePCPlus4ForRD_Data(UsePcPlus4ForRD_Data),
    .MemStore(MemStore), .Use0ForRD(Use0ForRD), .UsePCForALU_RS1(UsePcForALU_RS1),
    .Use0ForALU_RS1(Use0ForALU_RS1), .ALUCompOp(ALUCompOp), .SetPcLSBTo0(SetPcLSBTo0));
  RegisterFile registerfile_1 (
    .RS1(Instruction[19:15]), .RS2(Instruction[24:20]), .RD(multiplexer_2_out), .RD_Data(multiplexer_5_out),
    .Clk(Clk), .R1(R1), .R2(R2));
  Multiplexer #(.width(32)) multiplexer_6 (.in0(R1), .in1(PC), .out(multiplexer_6_out), .sel(UsePcForALU_RS1));
  Multiplexer #(.width(32)) multiplexer_7 (
    .in0(multiplexer_6_out), .out(multiplexer_7_out), .sel(Use0ForALU_RS1));  // open: in1
  ImmGen immgen_1 (.Instruction(Instruction), .ImmOut(immgen_1_immout));
  Multiplexer #(.width(32)) multiplexer_8 (.in0(R2), .in1(immgen_1_immout), .out(multiplexer_8_out), .sel(UseImm));
  ALU alu_1 (
    .RS1(multiplexer_7_out), .RS2(multiplexer_8_out), .ALUOperation(ALUOperation),
    .UseArithmeticRightShift(ALUArithmeticRightShift), .UseSubtract(ALUSub), .CompOp(ALUCompOp),
    .ALUOutput(ALUOutput), .CompResult(ALUCompResult));

  // Other names for the same wires on the sheet: RD[4:0] = Instruction[11:7]; RS1[4:0] = Instruction[19:15];
  //   RS2[4:0] = Instruction[24:20]

  // Notes on the sheet:
  //   The first rom instruction cannot be used !!
  //   The pc is measured in bytes, not words So it needs to be adjusted when used in rom addr
endmodule

module ALU (
  input  [31:0] RS1,
  input  [31:0] RS2,
  input  [2:0] ALUOperation,
  input  UseArithmeticRightShift,
  input  UseSubtract,
  input  [2:0] CompOp,
  output [31:0] ALUOutput,
  output CompResult
);

  wire comparator_1_lt, comparator_2_lt, comparator_3_eq, comparator_3_gt, comparator_3_lt, comparator_4_eq,
       comparator_4_gt, comparator_4_lt, not_1_out, or_2_out, or_3_out;
  wire [4:0] bit_extender_1_out, bit_extender_2_out;
  wire [31:0] adder_1_out, and_1_out, bit_extender_3_out, bit_extender_4_out, multiplexer_1_out,
       multiplexer_2_out, or_1_out, shifter_1_out, shifter_2_out, shifter_3_out, subtractor_1_out, xor_1_out;

  Bit_Extender #(.in_width(32), .out_width(5), .\type ("zero")) bit_extender_1 (.in(RS2), .out(bit_extender_1_out));
  Bit_Extender #(.in_width(32), .out_width(5), .\type ("zero")) bit_extender_2 (.in(RS2), .out(bit_extender_2_out));
  Shifter #(.width(32)) shifter_1 (.in(RS1), .\dist (bit_extender_1_out), .out(shifter_1_out));
  Adder #(.width(32)) adder_1 (.a(RS1), .b(RS2), .out(adder_1_out));  // open: cin, cout
  Subtractor #(.width(32)) subtractor_1 (.a(RS1), .b(RS2), .out(subtractor_1_out));  // open: bin, bout
  Comparator #(.width(32)) comparator_1 (.a(RS1), .b(RS2), .lt(comparator_1_lt));  // open: gt, eq
  Comparator #(.mode("unsigned"), .width(32)) comparator_2 (.a(RS1), .b(RS2), .lt(comparator_2_lt));  // open: gt, eq
  assign xor_1_out = RS1 ^ RS2;  // XOR_Gate xor_1, 32 bits wide
  assign or_1_out = RS1 | RS2;  // OR_Gate or_1, 32 bits wide
  assign and_1_out = RS1 & RS2;  // AND_Gate and_1, 32 bits wide
  Shifter #(.shift("lr"), .width(32)) shifter_2 (.in(RS1), .\dist (bit_extender_2_out), .out(shifter_2_out));
  Shifter #(.shift("ar"), .width(32)) shifter_3 (.in(RS1), .\dist (bit_extender_2_out), .out(shifter_3_out));
  Multiplexer #(.width(32)) multiplexer_1 (
    .in0(adder_1_out), .in1(subtractor_1_out), .out(multiplexer_1_out), .sel(UseSubtract));
  assign bit_extender_3_out = {{31{1'b0}}, comparator_1_lt};  // Bit_Extender bit_extender_3
  assign bit_extender_4_out = {{31{1'b0}}, comparator_2_lt};  // Bit_Extender bit_extender_4
  Multiplexer #(.width(32)) multiplexer_2 (
    .in0(shifter_2_out), .in1(shifter_3_out), .out(multiplexer_2_out), .sel(UseArithmeticRightShift));
  Multiplexer #(.select(3), .width(32)) multiplexer_3 (
    .in0(multiplexer_1_out), .in1(shifter_1_out), .in2(bit_extender_3_out), .in3(bit_extender_4_out),
    .in4(xor_1_out), .in5(multiplexer_2_out), .in6(or_1_out), .in7(and_1_out), .out(ALUOutput),
    .sel(ALUOperation));
  Comparator #(.width(32)) comparator_3 (
    .a(RS1), .b(RS2), .gt(comparator_3_gt), .eq(comparator_3_eq), .lt(comparator_3_lt));
  Comparator #(.mode("unsigned"), .width(32)) comparator_4 (
    .a(RS1), .b(RS2), .gt(comparator_4_gt), .eq(comparator_4_eq), .lt(comparator_4_lt));
  or or_2 (or_2_out, comparator_3_gt, comparator_3_eq);
  or or_3 (or_3_out, comparator_4_gt, comparator_4_eq);
  not not_1 (not_1_out, comparator_3_eq);
  Multiplexer #(.select(3)) multiplexer_4 (
    .in0(comparator_3_eq), .in1(not_1_out), .in2(1'b0), .in3(1'b1), .in4(comparator_3_lt), .in5(or_2_out),
    .in6(comparator_4_lt), .in7(or_3_out), .out(CompResult), .sel(CompOp));

  // Notes on the sheet:
  //   CompOp 010 always returns 0
  //   CompOp 011 always returns 1
endmodule

module RegisterFile (
  input  [4:0] RS1,
  input  [4:0] RS2,
  input  [4:0] RD,
  input  [31:0] RD_Data,
  input  Clk,
  output [31:0] R1,
  output [31:0] R2
);

  wire demultiplexer_1_out1, demultiplexer_1_out2, demultiplexer_1_out3, demultiplexer_1_out4,
       demultiplexer_1_out5, demultiplexer_1_out6, demultiplexer_1_out7, demultiplexer_1_out8,
       demultiplexer_1_out9, demultiplexer_1_out10, demultiplexer_1_out11, demultiplexer_1_out12,
       demultiplexer_1_out13, demultiplexer_1_out14, demultiplexer_1_out15, demultiplexer_1_out16,
       demultiplexer_1_out17, demultiplexer_1_out18, demultiplexer_1_out19, demultiplexer_1_out20,
       demultiplexer_1_out21, demultiplexer_1_out22, demultiplexer_1_out23, demultiplexer_1_out24,
       demultiplexer_1_out25, demultiplexer_1_out26, demultiplexer_1_out27, demultiplexer_1_out28,
       demultiplexer_1_out29, demultiplexer_1_out30, demultiplexer_1_out31;
  wire [31:0] register_1_q, register_2_q, register_3_q, register_4_q, register_5_q, register_6_q,
       register_7_q, register_8_q, register_9_q, register_10_q, register_11_q, register_12_q, register_13_q,
       register_14_q, register_15_q, register_16_q, register_17_q, register_18_q, register_19_q,
       register_20_q, register_21_q, register_22_q, register_23_q, register_24_q, register_25_q,
       register_26_q, register_27_q, register_28_q, register_29_q, register_30_q, register_31_q;

  Demultiplexer #(.select(5)) demultiplexer_1 (
    .out1(demultiplexer_1_out1), .out2(demultiplexer_1_out2), .out3(demultiplexer_1_out3),
    .out4(demultiplexer_1_out4), .out5(demultiplexer_1_out5), .out6(demultiplexer_1_out6),
    .out7(demultiplexer_1_out7), .out8(demultiplexer_1_out8), .out9(demultiplexer_1_out9),
    .out10(demultiplexer_1_out10), .out11(demultiplexer_1_out11), .out12(demultiplexer_1_out12),
    .out13(demultiplexer_1_out13), .out14(demultiplexer_1_out14), .out15(demultiplexer_1_out15),
    .out16(demultiplexer_1_out16), .out17(demultiplexer_1_out17), .out18(demultiplexer_1_out18),
    .out19(demultiplexer_1_out19), .out20(demultiplexer_1_out20), .out21(demultiplexer_1_out21),
    .out22(demultiplexer_1_out22), .out23(demultiplexer_1_out23), .out24(demultiplexer_1_out24),
    .out25(demultiplexer_1_out25), .out26(demultiplexer_1_out26), .out27(demultiplexer_1_out27),
    .out28(demultiplexer_1_out28), .out29(demultiplexer_1_out29), .out30(demultiplexer_1_out30),
    .out31(demultiplexer_1_out31), .in(1'b1), .sel(RD));  // open: out0
  Register #(.width(32)) register_1 (.D(RD_Data), .en(demultiplexer_1_out1), .clk(Clk), .Q(register_1_q));  // open: clr
  Register #(.width(32)) register_2 (.D(RD_Data), .en(demultiplexer_1_out2), .clk(Clk), .Q(register_2_q));  // open: clr
  Register #(.width(32)) register_3 (.D(RD_Data), .en(demultiplexer_1_out3), .clk(Clk), .Q(register_3_q));  // open: clr
  Register #(.width(32)) register_4 (.D(RD_Data), .en(demultiplexer_1_out4), .clk(Clk), .Q(register_4_q));  // open: clr
  Register #(.width(32)) register_5 (.D(RD_Data), .en(demultiplexer_1_out5), .clk(Clk), .Q(register_5_q));  // open: clr
  Register #(.width(32)) register_6 (.D(RD_Data), .en(demultiplexer_1_out6), .clk(Clk), .Q(register_6_q));  // open: clr
  Register #(.width(32)) register_7 (.D(RD_Data), .en(demultiplexer_1_out7), .clk(Clk), .Q(register_7_q));  // open: clr
  Register #(.width(32)) register_8 (.D(RD_Data), .en(demultiplexer_1_out8), .clk(Clk), .Q(register_8_q));  // open: clr
  Register #(.width(32)) register_9 (.D(RD_Data), .en(demultiplexer_1_out9), .clk(Clk), .Q(register_9_q));  // open: clr
  Register #(.width(32)) register_10 (
    .D(RD_Data), .en(demultiplexer_1_out10), .clk(Clk), .Q(register_10_q));  // open: clr
  Register #(.width(32)) register_11 (
    .D(RD_Data), .en(demultiplexer_1_out11), .clk(Clk), .Q(register_11_q));  // open: clr
  Register #(.width(32)) register_12 (
    .D(RD_Data), .en(demultiplexer_1_out12), .clk(Clk), .Q(register_12_q));  // open: clr
  Register #(.width(32)) register_13 (
    .D(RD_Data), .en(demultiplexer_1_out13), .clk(Clk), .Q(register_13_q));  // open: clr
  Register #(.width(32)) register_14 (
    .D(RD_Data), .en(demultiplexer_1_out14), .clk(Clk), .Q(register_14_q));  // open: clr
  Register #(.width(32)) register_15 (
    .D(RD_Data), .en(demultiplexer_1_out15), .clk(Clk), .Q(register_15_q));  // open: clr
  Register #(.width(32)) register_16 (
    .D(RD_Data), .en(demultiplexer_1_out16), .clk(Clk), .Q(register_16_q));  // open: clr
  Register #(.width(32)) register_17 (
    .D(RD_Data), .en(demultiplexer_1_out17), .clk(Clk), .Q(register_17_q));  // open: clr
  Register #(.width(32)) register_18 (
    .D(RD_Data), .en(demultiplexer_1_out18), .clk(Clk), .Q(register_18_q));  // open: clr
  Register #(.width(32)) register_19 (
    .D(RD_Data), .en(demultiplexer_1_out19), .clk(Clk), .Q(register_19_q));  // open: clr
  Register #(.width(32)) register_20 (
    .D(RD_Data), .en(demultiplexer_1_out20), .clk(Clk), .Q(register_20_q));  // open: clr
  Register #(.width(32)) register_21 (
    .D(RD_Data), .en(demultiplexer_1_out21), .clk(Clk), .Q(register_21_q));  // open: clr
  Register #(.width(32)) register_22 (
    .D(RD_Data), .en(demultiplexer_1_out22), .clk(Clk), .Q(register_22_q));  // open: clr
  Register #(.width(32)) register_23 (
    .D(RD_Data), .en(demultiplexer_1_out23), .clk(Clk), .Q(register_23_q));  // open: clr
  Register #(.width(32)) register_24 (
    .D(RD_Data), .en(demultiplexer_1_out24), .clk(Clk), .Q(register_24_q));  // open: clr
  Register #(.width(32)) register_25 (
    .D(RD_Data), .en(demultiplexer_1_out25), .clk(Clk), .Q(register_25_q));  // open: clr
  Register #(.width(32)) register_26 (
    .D(RD_Data), .en(demultiplexer_1_out26), .clk(Clk), .Q(register_26_q));  // open: clr
  Register #(.width(32)) register_27 (
    .D(RD_Data), .en(demultiplexer_1_out27), .clk(Clk), .Q(register_27_q));  // open: clr
  Register #(.width(32)) register_28 (
    .D(RD_Data), .en(demultiplexer_1_out28), .clk(Clk), .Q(register_28_q));  // open: clr
  Register #(.width(32)) register_29 (
    .D(RD_Data), .en(demultiplexer_1_out29), .clk(Clk), .Q(register_29_q));  // open: clr
  Register #(.width(32)) register_30 (
    .D(RD_Data), .en(demultiplexer_1_out30), .clk(Clk), .Q(register_30_q));  // open: clr
  Register #(.width(32)) register_31 (
    .D(RD_Data), .en(demultiplexer_1_out31), .clk(Clk), .Q(register_31_q));  // open: clr
  Multiplexer #(.select(5), .width(32)) multiplexer_1 (
    .in0({32{1'b0}}), .in1(register_1_q), .in2(register_2_q), .in3(register_3_q), .in4(register_4_q),
    .in5(register_5_q), .in6(register_6_q), .in7(register_7_q), .in8(register_8_q), .in9(register_9_q),
    .in10(register_10_q), .in11(register_11_q), .in12(register_12_q), .in13(register_13_q),
    .in14(register_14_q), .in15(register_15_q), .in16(register_16_q), .in17(register_17_q),
    .in18(register_18_q), .in19(register_19_q), .in20(register_20_q), .in21(register_21_q),
    .in22(register_22_q), .in23(register_23_q), .in24(register_24_q), .in25(register_25_q),
    .in26(register_26_q), .in27(register_27_q), .in28(register_28_q), .in29(register_29_q),
    .in30(register_30_q), .in31(register_31_q), .out(R1), .sel(RS1));
  Multiplexer #(.select(5), .width(32)) multiplexer_2 (
    .in0({32{1'b0}}), .in1(register_1_q), .in2(register_2_q), .in3(register_3_q), .in4(register_4_q),
    .in5(register_5_q), .in6(register_6_q), .in7(register_7_q), .in8(register_8_q), .in9(register_9_q),
    .in10(register_10_q), .in11(register_11_q), .in12(register_12_q), .in13(register_13_q),
    .in14(register_14_q), .in15(register_15_q), .in16(register_16_q), .in17(register_17_q),
    .in18(register_18_q), .in19(register_19_q), .in20(register_20_q), .in21(register_21_q),
    .in22(register_22_q), .in23(register_23_q), .in24(register_24_q), .in25(register_25_q),
    .in26(register_26_q), .in27(register_27_q), .in28(register_28_q), .in29(register_29_q),
    .in30(register_30_q), .in31(register_31_q), .out(R2), .sel(RS2));

  // Notes on the sheet:
  //   R0 is hard wired to 0
endmodule

module ControlLogic (
  input  [31:0] Instruction,
  output [2:0] ALUOp,
  output UseImm,
  output ALUArithmeticShift,
  output ALUSub,
  output MemLoad,
  output UseMemInForRD_Data,
  output UsePCPlus4ForRD_Data,
  output MemStore,
  output Use0ForRD,
  output UsePCForALU_RS1,
  output Use0ForALU_RS1,
  output [2:0] ALUCompOp,
  output SetPcLSBTo0
);

  wire comparator_2_eq, IsAUIPCInstr, IsBranchInstr, IsIInstr, IsJALInstr, IsLUIInstr, IsRInstr, IsUInstr,
       or_2_out, or_6_out;
  wire [2:0] multiplexer_1_out;

  Comparator #(.width(5)) comparator_1 (.a(Instruction[6:2]), .b(5'b01101), .eq(IsLUIInstr));  // open: gt, lt
  Comparator #(.width(5)) comparator_2 (.a(Instruction[6:2]), .b(5'b00101), .eq(comparator_2_eq));  // open: gt, lt
  or or_1 (Use0ForALU_RS1, IsJALInstr, SetPcLSBTo0, IsLUIInstr);
  Multiplexer #(.width(3)) multiplexer_1 (
    .in0(3'b010), .in1(Instruction[14:12]), .out(multiplexer_1_out), .sel(IsBranchInstr));
  Comparator #(.width(5)) comparator_3 (.a(Instruction[6:2]), .b(5'b00101), .eq(IsAUIPCInstr));  // open: gt, lt
  Comparator #(.mode("unsigned"), .width(5)) comparator_4 (
    .a(Instruction[6:2]), .b({5{1'b0}}), .eq(MemLoad));  // open: gt, lt
  Comparator #(.mode("unsigned"), .width(5)) comparator_5 (
    .a(Instruction[6:2]), .b(5'b01000), .eq(MemStore));  // open: gt, lt
  Comparator #(.width(5)) comparator_6 (.a(Instruction[6:2]), .b(5'b11011), .eq(IsJALInstr));  // open: gt, lt
  Comparator #(.width(5)) comparator_7 (.a(Instruction[6:2]), .b(5'b11001), .eq(SetPcLSBTo0));  // open: gt, lt
  Comparator #(.width(5)) comparator_8 (.a(Instruction[6:2]), .b(5'b11000), .eq(IsBranchInstr));  // open: gt, lt
  Comparator #(.mode("unsigned"), .width(5)) comparator_9 (
    .a(Instruction[6:2]), .b(5'b01100), .eq(IsRInstr));  // open: gt, lt
  Comparator #(.mode("unsigned"), .width(5)) comparator_10 (
    .a(Instruction[6:2]), .b(5'b00100), .eq(IsIInstr));  // open: gt, lt
  Multiplexer #(.width(3)) multiplexer_2 (.in0(3'b000), .in1(Instruction[14:12]), .out(ALUOp), .sel(or_2_out));
  or or_2 (or_2_out, IsRInstr, IsIInstr);
  not not_1 (UseImm, IsRInstr);
  and and_1 (ALUArithmeticShift, Instruction[30], IsRInstr);
  or or_3 (UsePCPlus4ForRD_Data, IsJALInstr, SetPcLSBTo0);
  or or_4 (IsUInstr, IsLUIInstr, comparator_2_eq);
  or or_5 (UsePCForALU_RS1, IsAUIPCInstr, IsBranchInstr);
  Multiplexer #(.width(3)) multiplexer_3 (.in0(multiplexer_1_out), .in1(3'b011), .out(ALUCompOp), .sel(or_6_out));
  or or_6 (or_6_out, SetPcLSBTo0, IsJALInstr);

  assign ALUSub = ALUArithmeticShift;
  assign Use0ForRD = MemStore;
  assign UseMemInForRD_Data = MemLoad;

  // Other names for the same wires on the sheet: funct_3[2:0] = Instruction[14:12]; IsJALRInstr = SetPcLSBTo0;
  //   IsLoadInstr = MemLoad; IsStoreInstr = MemStore; Opcode_2_to_6[4:0] = Instruction[6:2]

  // Notes on the sheet:
  //   CompOp 010 / 0x2 always returns 0
  //   CompOp 011 / 0x3 always returns 1
  //   Using the same register in JALR rs1 and rd is undefined behaviour. The correct implementation requires a temporary variable to first store pc + 4, set pc and finally set rd to pc+ 4 !!!
endmodule

module ImmGen (
  input  [31:0] Instruction,
  output [31:0] ImmOut
);

  wire comparator_5_eq, comparator_6_eq, IsBranchInstr, IsJALInstr, IsJALRInstr, IsStoreInstr, IsUInstr;
  wire [19:0] shifter_1_out;
  wire [31:0] ImmBranchType, ImmIType, ImmJALType, ImmSType, ImmUType, multiplexer_1_out, multiplexer_2_out,
       multiplexer_3_out;

  Shifter #(.width(20)) shifter_1 (.in(Instruction[31:12]), .\dist (5'b01100), .out(shifter_1_out));
  assign ImmUType = {{12{1'b0}}, shifter_1_out};  // Bit_Extender bit_extender_1
  assign ImmJALType = {{11{Instruction[31]}}, {Instruction[31], Instruction[19:12], Instruction[20], Instruction[30:21], 1'b0}};  // Bit_Extender bit_extender_2
  assign ImmSType = {{20{Instruction[31]}}, {Instruction[31:25], Instruction[11:7]}};  // Bit_Extender bit_extender_3
  assign ImmIType = {{20{Instruction[31]}}, Instruction[31:20]};  // Bit_Extender bit_extender_4
  assign ImmBranchType = {{19{Instruction[7]}}, {Instruction[7], Instruction[31:25], Instruction[11:8], 1'b0}};  // Bit_Extender bit_extender_5
  Multiplexer #(.width(32)) multiplexer_1 (.in0(ImmIType), .in1(ImmSType), .out(multiplexer_1_out), .sel(IsStoreInstr));
  Comparator #(.mode("unsigned"), .width(5)) comparator_1 (
    .a(Instruction[6:2]), .b(5'b01000), .eq(IsStoreInstr));  // open: gt, lt
  Comparator #(.width(5)) comparator_2 (.a(Instruction[6:2]), .b(5'b11000), .eq(IsBranchInstr));  // open: gt, lt
  Comparator #(.width(5)) comparator_3 (.a(Instruction[6:2]), .b(5'b11011), .eq(IsJALInstr));  // open: gt, lt
  Comparator #(.width(5)) comparator_4 (.a(Instruction[6:2]), .b(5'b11001), .eq(IsJALRInstr));  // open: gt, lt
  Comparator #(.width(5)) comparator_5 (.a(Instruction[6:2]), .b(5'b01101), .eq(comparator_5_eq));  // open: gt, lt
  Comparator #(.width(5)) comparator_6 (.a(Instruction[6:2]), .b(5'b00101), .eq(comparator_6_eq));  // open: gt, lt
  or or_1 (IsUInstr, comparator_5_eq, comparator_6_eq);
  Multiplexer #(.width(32)) multiplexer_2 (
    .in0(multiplexer_1_out), .in1(ImmUType), .out(multiplexer_2_out), .sel(IsUInstr));
  Multiplexer #(.width(32)) multiplexer_3 (
    .in0(multiplexer_2_out), .in1(ImmJALType), .out(multiplexer_3_out), .sel(IsJALInstr));
  Multiplexer #(.width(32)) multiplexer_4 (
    .in0(multiplexer_3_out), .in1(ImmBranchType), .out(ImmOut), .sel(IsBranchInstr));

  // Other names for the same wires on the sheet: Opcode[4:0] = Instruction[6:2]
endmodule

module ExtendMemInput (
  input  [31:0] Instruction,
  input  [31:0] MemIn,
  output [31:0] MemExtended
);

  wire [31:0] bit_extender_1_out, bit_extender_2_out, bit_extender_3_out, bit_extender_4_out,
       bit_extender_5_out;

  assign bit_extender_1_out = {{24{MemIn[7]}}, MemIn[7:0]};  // Bit_Extender bit_extender_1
  assign bit_extender_2_out = {{16{MemIn[15]}}, MemIn[15:0]};  // Bit_Extender bit_extender_2
  Bit_Extender #(.in_width(32), .out_width(32)) bit_extender_3 (.in(MemIn), .out(bit_extender_3_out));
  assign bit_extender_4_out = {{24{1'b0}}, MemIn[7:0]};  // Bit_Extender bit_extender_4
  assign bit_extender_5_out = {{16{1'b0}}, MemIn[15:0]};  // Bit_Extender bit_extender_5
  Multiplexer #(.select(3), .width(32)) multiplexer_1 (
    .in0(bit_extender_1_out), .in1(bit_extender_2_out), .in2(bit_extender_3_out), .in4(bit_extender_4_out),
    .in5(bit_extender_5_out), .out(MemExtended), .sel(Instruction[14:12]));  // open: in3, in6, in7

  // Other names for the same wires on the sheet: Sel[2:0] = Instruction[14:12]
endmodule

module PCLogic (
  input  [31:0] PCPrev,
  input  SetPcToOffset,
  input  AddOffsetToPc,
  input  [31:0] Instr,
  input  ALUCompResult,
  input  [31:0] PC_Offset,
  output [31:0] PCNew
);

  wire [31:0] adder_1_out, adder_2_out, multiplexer_1_out, multiplexer_2_out;

  Adder #(.width(32)) adder_1 (.a(PCPrev), .b(32'h4), .out(adder_1_out));  // open: cin, cout
  Adder #(.width(32)) adder_2 (.a(PCPrev), .b(PC_Offset), .out(adder_2_out));  // open: cin, cout
  Multiplexer #(.width(32)) multiplexer_1 (
    .in0(adder_2_out), .in1(PCPrev), .out(multiplexer_1_out), .sel(ALUCompResult));
  Multiplexer #(.width(32)) multiplexer_2 (
    .in0(adder_1_out), .in1(multiplexer_1_out), .out(multiplexer_2_out), .sel(AddOffsetToPc));
  Multiplexer #(.width(32)) multiplexer_3 (.in0(multiplexer_2_out), .in1(PC_Offset), .out(PCNew), .sel(SetPcToOffset));

  // Other names for the same wires on the sheet: Offset[31:0] = PC_Offset
endmodule
